// Digital circuit lotec.dig as structural Verilog
module lotec (
  input  clk,
  output [16:0] out_2,
  output [15:0] out_3,
  output [4:0] out_4,
  output [2:0] out_5,
  output [7:0] out_6,
  output [7:0] out_7,
  output [15:0] out_8,
  output [7:0] out_9,
  output out_10,
  output out_11,
  output out_12,
  output out_13,
  output [7:0] out_14,
  output [7:0] out_15,
  output [7:0] out_16,
  output [16:0] out_17,
  output [7:0] out_18
);

  wire add_1_c_o, ALU_ADD, ALU_AND, ALU_CMP, ALU_OR, ALU_SHL, ALU_SHR, ALU_SUB, ALU_XOR, ALUOUT, and_1_out,
       and_2_out, and_5_out, and_6_out, and_7_out, and_8_out, and_9_out, and_10_out, and_11_out, and_12_out,
       and_15_out, and_16_out, and_17_out, and_18_out, and_19_out, BRANCH_ALU, BRANCH_S0, BRANCH_S1,
       CARRYBUS, CARRYOUT, CLK1, CLK2, COND_AL, COND_EQ, COND_GE, COND_GT, COND_LE, COND_LT, COND_NE,
       COND_NV, nRST, OP_ADD, OP_ADDI, OP_AND, OP_ANDI, OP_BRANCH, OP_CMP, OP_CMPI, OP_JUMP, OP_LDB, OP_LI,
       OP_MOV, OP_NOP, OP_OR, OP_ORI, OP_SHL, OP_SHLI, OP_SHR, OP_SHRI, OP_STB, OP_SUB, OP_SUBI, OP_XOR,
       OP_XORI, or_1_out, or_2_out, or_3_out, or_4_out, or_7_out, or_8_out, or_10_out, or_11_out, or_12_out,
       RD_FLAGS, RD_R0, RD_R1, RD_R2, RD_R3, RD_R4, REGEN, sub_1_c_o;
  wire [1:0] Clock_Devider_out, priorityencoder_1_num, priorityencoder_2_num, RD_PC;
  wire [3:1] comparator_1_gt;
  wire [4:0] SHLVALUE, SHRVALUE;
  wire [7:0] add_1_s, ALUOP1, ALUOP2, and_3_out, multiplexer_1_out, or_6_out, ramasync_1_q, RSVALUE, RTVALUE,
       sub_1_s, xor_1_out;
  wire [15:0] add_2_s, ADRESSBUS, bitextender_2_out, multiplexer_2_out, multiplexer_8_out, PC_ALU;
  wire [17:0] barrelshifter_1_out, barrelshifter_2_out;

  Comparator #(.Bits(8)) comparator_1 (
    .a(ALUOP1), .b(ALUOP2), .gt(comparator_1_gt[1]), .eq(comparator_1_gt[2]), .lt(comparator_1_gt[3]));
  and and_1 (and_1_out, REGEN, RD_FLAGS);
  Multiplexer #(.Bits(8)) multiplexer_1 (
    .sel(and_1_out), .in_0({4'b0000, comparator_1_gt, CARRYBUS}), .in_1(PC_ALU[7:0]), .out(multiplexer_1_out));
  or or_1 (or_1_out, CARRYOUT, and_1_out);
  or or_2 (or_2_out, ALU_CMP, and_1_out);
  or or_3 (or_3_out, ALU_CMP, and_1_out);
  or or_4 (or_4_out, ALU_CMP, and_1_out);
  ROM #(.AddrBits(16), .Bits(16)) rom_1 (.A(out_2[16:1]), .sel(1'b1), .D(out_8));
  Decoder #(.Selector_Bits(5)) decoder_1 (
    .sel(out_3[15:11]), .out_0(OP_NOP), .out_1(OP_LI), .out_2(OP_ADDI), .out_3(OP_ANDI), .out_4(OP_ORI),
    .out_5(OP_XORI), .out_6(OP_SUBI), .out_7(OP_CMPI), .out_8(OP_SHRI), .out_9(OP_SHLI), .out_17(OP_MOV),
    .out_18(OP_ADD), .out_19(OP_AND), .out_20(OP_OR), .out_21(OP_XOR), .out_22(OP_SUB), .out_23(OP_CMP),
    .out_24(OP_SHR), .out_25(OP_SHL), .out_28(OP_LDB), .out_29(OP_STB), .out_30(OP_JUMP), .out_31(OP_BRANCH));  // open: out_10, out_11, out_12, out_13, out_14, out_15, out_16, out_26, out_27
  Register Carryflag (.D(multiplexer_1_out[0]), .C(CLK2), .en(or_1_out), .Q(out_10));
  Register Greaterflag (.D(multiplexer_1_out[1]), .C(CLK2), .en(or_2_out), .Q(out_12));
  Register Equalflag (.D(multiplexer_1_out[2]), .C(CLK2), .en(or_3_out), .Q(out_11));
  Register Lessflag (.D(multiplexer_1_out[3]), .C(CLK2), .en(or_4_out), .Q(out_13));
  Decoder #(.Selector_Bits(3)) decoder_2 (
    .sel(out_3[10:8]), .out_0(RD_R0), .out_1(RD_R1), .out_2(RD_R2), .out_3(RD_R3), .out_4(RD_R4),
    .out_5(RD_FLAGS), .out_6(RD_PC[0]), .out_7(RD_PC[1]));
  Multiplexer #(.Bits(16)) multiplexer_2 (.sel(BRANCH_S1), .in_0(out_8), .in_1({16{1'b0}}), .out(multiplexer_2_out));
  and and_2 (and_2_out, OP_STB, CLK2);
  or or_5 (REGEN, ALUOUT, OP_LI, OP_LDB, OP_MOV);
  Decoder #(.Selector_Bits(3)) decoder_3 (
    .sel(out_3[10:8]), .out_0(COND_AL), .out_1(COND_EQ), .out_2(COND_GT), .out_3(COND_LT), .out_4(COND_NE),
    .out_5(COND_GE), .out_6(COND_LE), .out_7(COND_NV));
  CounterPreset #(.Bits(16)) Programcounter (
    .en(1'b1), .C(CLK1), .dir(1'b0), .in(out_17[16:1]), .ld(BRANCH_S1), .clr(nRST), .out(out_2[16:1]));  // open: ovf
  D_FF #(.Bits(16)) Instruction_Register (.D(multiplexer_2_out), .C(CLK1), .Q(out_3));  // open: nQ
  RAMAsync #(.AddrBits(16), .Bits(8)) ramasync_1 (.A(ADRESSBUS), .D(ALUOP1), .we(and_2_out), .Q(ramasync_1_q));
  Add #(.Bits(8)) add_1 (.a(ALUOP1), .b(ALUOP2), .c_i(out_10), .s(add_1_s), .c_o(add_1_c_o));
  assign and_3_out = ALUOP1 & ALUOP2;  // And and_3, 8 bits wide
  assign or_6_out = ALUOP1 | ALUOP2;  // Or or_6, 8 bits wide
  assign xor_1_out = ALUOP1 ^ ALUOP2;  // XOr xor_1, 8 bits wide
  Sub #(.Bits(8)) sub_1 (.a(ALUOP1), .b(ALUOP2), .c_i(out_10), .s(sub_1_s), .c_o(sub_1_c_o));
  Multiplexer #(.Selector_Bits(3), .Bits(8)) multiplexer_3 (
    .sel(out_3[7:5]), .in_0(out_7), .in_1(out_14), .in_2(out_15), .in_3(out_16), .in_4(out_18),
    .in_5({4'b0000, out_13, out_11, out_12, out_10}), .in_6(out_2[8:1]), .in_7(out_2[16:9]), .out(RSVALUE));
  BarrelShifter #(.Bits(18)) barrelshifter_1 (
    .in({1'b0, ALUOP1, RSVALUE, out_10}), .shift(SHLVALUE), .out(barrelshifter_1_out));
  and and_4 (BRANCH_ALU, REGEN, RD_PC[0]);
  and and_5 (and_5_out, RD_PC[1], REGEN);
  BitExtender bitextender_1 (.in(out_3[7:0]), .out(ADRESSBUS));
  or or_7 (or_7_out, out_12, out_11);
  or or_8 (or_8_out, out_13, out_11);
  BitExtender bitextender_2 (.in(out_3[7:0]), .out(bitextender_2_out));
  PriorityEncoder #(.Selector_Bits(2)) priorityencoder_1 (
    .in0(ALUOUT), .in1(OP_LI), .in2(OP_LDB), .in3(OP_MOV), .num(priorityencoder_1_num));  // open: any
  assign out_9 = ALU_ADD ? add_1_s : 8'bz;  // Driver driver_1
  assign out_9 = ALU_AND ? and_3_out : 8'bz;  // Driver driver_2
  assign out_9 = ALU_OR ? or_6_out : 8'bz;  // Driver driver_3
  assign out_9 = ALU_XOR ? xor_1_out : 8'bz;  // Driver driver_4
  assign out_9 = ALU_SUB ? sub_1_s : 8'bz;  // Driver driver_5
  Multiplexer #(.Selector_Bits(2), .Bits(8)) multiplexer_4 (
    .sel(priorityencoder_1_num), .in_0(out_9), .in_1(out_3[7:0]), .in_2(ramasync_1_q), .in_3(RSVALUE),
    .out(PC_ALU[7:0]));
  Multiplexer #(.Bits(5)) multiplexer_5 (.sel(OP_SHLI), .in_0(RTVALUE[4:0]), .in_1(out_3[4:0]), .out(SHLVALUE));
  Multiplexer #(.Bits(5)) multiplexer_6 (.sel(OP_SHRI), .in_0(RTVALUE[4:0]), .in_1(out_3[4:0]), .out(SHRVALUE));
  or or_9 (ALUOUT, ALU_ADD, ALU_AND, ALU_OR, ALU_XOR, ALU_SUB, ALU_SHL, ALU_SHR);
  Add #(.Bits(16)) add_2 (.a(out_2[16:1]), .b(bitextender_2_out), .c_i(1'b0), .s(add_2_s));  // open: c_o
  assign CARRYBUS = ALU_ADD ? add_1_c_o : 1'bz;  // Driver driver_6
  assign CARRYBUS = ALU_SUB ? sub_1_c_o : 1'bz;  // Driver driver_7
  assign out_9 = ALU_SHL ? barrelshifter_1_out[16:9] : 8'bz;  // Driver driver_8
  assign CARRYBUS = ALU_SHL ? barrelshifter_1_out[17] : 1'bz;  // Driver driver_9
  Register #(.Bits(8)) PCH (.D(PC_ALU[7:0]), .C(CLK2), .en(and_5_out), .Q(PC_ALU[15:8]));
  and and_6 (and_6_out, COND_EQ, out_11);
  and and_7 (and_7_out, COND_GT, out_12);
  and and_8 (and_8_out, COND_LT, out_13);
  and and_9 (and_9_out, COND_NE, ~out_11);  // And
  and and_10 (and_10_out, COND_GE, or_7_out);
  and and_11 (and_11_out, COND_LE, or_8_out);
  or or_10 (or_10_out, OP_LI, OP_ADDI, OP_ANDI, OP_ORI, OP_XORI, OP_SUBI, OP_CMPI);
  PriorityEncoder #(.Selector_Bits(2)) priorityencoder_2 (
    .in0(OP_JUMP), .in1(OP_BRANCH), .in2(BRANCH_ALU), .in3(1'b0), .num(priorityencoder_2_num));  // open: any
  Reset #(.invertOutput("false")) reset_1 (.out(nRST));
  Multiplexer #(.Selector_Bits(3), .Bits(8)) multiplexer_7 (
    .sel(out_3[10:8]), .in_0(out_7), .in_1(out_14), .in_2(out_15), .in_3(out_16), .in_4(out_18),
    .in_5({4'b0000, out_13, out_11, out_12, out_10}), .in_6(out_2[8:1]), .in_7(out_2[16:9]), .out(ALUOP1));
  Multiplexer #(.Selector_Bits(2), .Bits(16)) multiplexer_8 (
    .sel(priorityencoder_2_num), .in_0({RSVALUE, RTVALUE}), .in_1(add_2_s), .in_2(PC_ALU), .in_3({16{1'b0}}),
    .out(multiplexer_8_out));
  Counter #(.Bits(2)) Clock_Devider (.en(1'b1), .C(clk), .clr(1'b0), .out(Clock_Devider_out));  // open: ovf
  or or_11 (or_11_out, OP_JUMP, OP_BRANCH);
  or or_12 (or_12_out, COND_AL, and_6_out, and_7_out, and_8_out, and_9_out, and_10_out, and_11_out);
  Multiplexer #(.Bits(8)) multiplexer_9 (.sel(or_10_out), .in_0(RSVALUE), .in_1(out_3[7:0]), .out(ALUOP2));
  or or_13 (ALU_SHL, OP_SHLI, OP_SHL);
  or or_14 (ALU_SHR, OP_SHRI, OP_SHR);
  or or_15 (CARRYOUT, OP_ADDI, OP_SUBI, ALU_SHL, ALU_SHR);
  and and_12 (and_12_out, or_11_out, or_12_out);
  and and_13 (CLK1, ~Clock_Devider_out[1], ~Clock_Devider_out[0]);  // And
  Register Branch (.D(BRANCH_S0), .C(CLK2), .en(1'b1), .Q(BRANCH_S1));
  Register #(.Bits(16)) Branch_Target (.D(multiplexer_8_out), .C(CLK2), .en(BRANCH_S0), .Q(out_17[16:1]));
  and and_14 (CLK2, ~Clock_Devider_out[0], Clock_Devider_out[1]);  // And
  and and_15 (and_15_out, REGEN, RD_R0);
  and and_16 (and_16_out, REGEN, RD_R1);
  and and_17 (and_17_out, REGEN, RD_R2);
  and and_18 (and_18_out, REGEN, RD_R3);
  and and_19 (and_19_out, REGEN, RD_R4);
  BarrelShifter #(.Bits(18), .direction("right")) barrelshifter_2 (
    .in({out_10, RSVALUE, ALUOP1, 1'b0}), .shift(SHRVALUE), .out(barrelshifter_2_out));
  or or_16 (BRANCH_S0, BRANCH_ALU, and_12_out);
  Multiplexer #(.Selector_Bits(3), .Bits(8)) multiplexer_10 (
    .sel(out_3[4:2]), .in_0(out_7), .in_1(out_14), .in_2(out_15), .in_3(out_16), .in_4(out_18),
    .in_5({4'b0000, out_13, out_11, out_12, out_10}), .in_6(out_2[8:1]), .in_7(out_2[16:9]), .out(RTVALUE));
  Register #(.Bits(8)) R0 (.D(PC_ALU[7:0]), .C(CLK2), .en(and_15_out), .Q(out_7));
  Register #(.Bits(8)) R1 (.D(PC_ALU[7:0]), .C(CLK2), .en(and_16_out), .Q(out_14));
  Register #(.Bits(8)) R2 (.D(PC_ALU[7:0]), .C(CLK2), .en(and_17_out), .Q(out_15));
  Register #(.Bits(8)) R3 (.D(PC_ALU[7:0]), .C(CLK2), .en(and_18_out), .Q(out_16));
  Register #(.Bits(8)) R4 (.D(PC_ALU[7:0]), .C(CLK2), .en(and_19_out), .Q(out_18));
  assign CARRYBUS = ALU_SHR ? barrelshifter_2_out[0] : 1'bz;  // Driver driver_10
  assign out_9 = ALU_SHR ? barrelshifter_2_out[8:1] : 8'bz;  // Driver driver_11
  or or_17 (ALU_ADD, OP_ADD, OP_ADDI);
  or or_18 (ALU_AND, OP_AND, OP_ANDI);
  or or_19 (ALU_OR, OP_OR, OP_ORI);
  or or_20 (ALU_XOR, OP_XOR, OP_XORI);
  or or_21 (ALU_SUB, OP_SUB, OP_SUBI);
  or or_22 (ALU_CMP, OP_CMP, OP_CMPI);

  assign out_2[0] = 1'b0;
  assign out_4 = out_3[15:11];
  assign out_5 = out_3[10:8];
  assign out_6 = out_3[7:0];
  assign out_17[0] = 1'b0;

  // Other names for the same wires on the sheet: ALUBUS[7:0] = out_9; BRANCHTARGETBUS[15:0] = out_17[16:1];
  //   CARRYFLAG = out_10; FLAGBUS[3:0] = {out_13, out_11, out_12, out_10}; EQFLAGBUS = out_11; GTFLAGBUS = out_12;
  //   IMM2[1:0] = out_3[1:0]; IMM5[4:0] = out_3[4:0]; IMM8[7:0] = out_3[7:0]; IMM11[10:0] = out_3[10:0];
  //   IRBUS[15:0] = out_3; RT[2:0] = out_3[4:2]; RS[2:0] = out_3[7:5]; COND[2:0] = out_3[10:8]; RD[2:0] = out_3[10:8];
  //   OPCODE[4:0] = out_3[15:11]; LTFLAGBUS = out_13; PCBUS[15:0] = out_2[16:1]; PCDATABUS[15:0] = out_8;
  //   R0BUS[7:0] = out_7; R1BUS[7:0] = out_14; R2BUS[7:0] = out_15; R3BUS[7:0] = out_16; R4BUS[7:0] = out_18;
  //   REGVAL[7:0] = PC_ALU[7:0]

  // Notes on the sheet:
  //   clk: Hz: 5
  //   contents of rom_1 (hex, n*v repeats v):
  //   808,980,4809,4009,4801,4001,c028,c008,c828,c808,f00,e11,4*0,f8ff
  //   ,800,91a,8f00,8e20,4*0,f8ff,800,92b,f004,13*0,f8ff,dff,88a0,d08
  //   ,88a0,d04,88a0,d02,88a0,d01,88a0,d00,88a0,dff,980,a01,b01,c94c
  //   ,800,901,a00,d00,9020,d00,1201,3a05,fbfa,840,941,a42,b43,c44,8860
  //   ,8940,842,952,a43,b53,8a00,8b20,820,921,a22,b23,c23,f8ff
endmodule
